// Logisim project memoryless.circ as structural Verilog: 1 circuit, main circuit main
module main (
  input  [7:0] A,
  input  [7:0] B,
  output [15:0] Result
);

  wire [15:0] adder_1_out, adder_2_out, adder_3_out, adder_4_out, adder_5_out, adder_6_out,
       multiplexer_1_out, multiplexer_2_out, multiplexer_3_out, multiplexer_4_out, multiplexer_5_out,
       multiplexer_6_out, multiplexer_7_out, multiplexer_8_out, shifter_1_out, shifter_2_out, shifter_3_out,
       shifter_4_out, shifter_5_out, shifter_6_out, shifter_7_out;

  Shifter #(.width(16)) shifter_1 (.in({{8{1'b0}}, A}), .\dist (4'b0001), .out(shifter_1_out));
  Shifter #(.width(16)) shifter_2 (.in({{8{1'b0}}, A}), .\dist (4'b0010), .out(shifter_2_out));
  Shifter #(.width(16)) shifter_3 (.in({{8{1'b0}}, A}), .\dist (4'b0011), .out(shifter_3_out));
  Shifter #(.width(16)) shifter_4 (.in({{8{1'b0}}, A}), .\dist (4'b0100), .out(shifter_4_out));
  Shifter #(.width(16)) shifter_5 (.in({{8{1'b0}}, A}), .\dist (4'b0101), .out(shifter_5_out));
  Shifter #(.width(16)) shifter_6 (.in({{8{1'b0}}, A}), .\dist (4'b0110), .out(shifter_6_out));
  Shifter #(.width(16)) shifter_7 (.in({{8{1'b0}}, A}), .\dist (4'b0111), .out(shifter_7_out));
  Multiplexer #(.width(16), .enable("false")) multiplexer_1 (
    .in0({16{1'b0}}), .in1({{8{1'b0}}, A}), .out(multiplexer_1_out), .sel(B[0]));
  Multiplexer #(.width(16), .enable("false")) multiplexer_2 (
    .in0({16{1'b0}}), .in1(shifter_1_out), .out(multiplexer_2_out), .sel(B[1]));
  Multiplexer #(.width(16), .enable("false")) multiplexer_3 (
    .in0({16{1'b0}}), .in1(shifter_2_out), .out(multiplexer_3_out), .sel(B[2]));
  Multiplexer #(.width(16), .enable("false")) multiplexer_4 (
    .in0({16{1'b0}}), .in1(shifter_3_out), .out(multiplexer_4_out), .sel(B[3]));
  Multiplexer #(.width(16), .enable("false")) multiplexer_5 (
    .in0({16{1'b0}}), .in1(shifter_4_out), .out(multiplexer_5_out), .sel(B[4]));
  Multiplexer #(.width(16), .enable("false")) multiplexer_6 (
    .in0({16{1'b0}}), .in1(shifter_5_out), .out(multiplexer_6_out), .sel(B[5]));
  Multiplexer #(.width(16), .enable("false")) multiplexer_7 (
    .in0({16{1'b0}}), .in1(shifter_6_out), .out(multiplexer_7_out), .sel(B[6]));
  Multiplexer #(.width(16), .enable("false")) multiplexer_8 (
    .in0({16{1'b0}}), .in1(shifter_7_out), .out(multiplexer_8_out), .sel(B[7]));
  Adder #(.width(16)) adder_1 (.a(multiplexer_1_out), .b(multiplexer_2_out), .out(adder_1_out));  // open: cin, cout
  Adder #(.width(16)) adder_2 (.a(multiplexer_3_out), .b(multiplexer_4_out), .out(adder_2_out));  // open: cin, cout
  Adder #(.width(16)) adder_3 (.a(multiplexer_5_out), .b(multiplexer_6_out), .out(adder_3_out));  // open: cin, cout
  Adder #(.width(16)) adder_4 (.a(multiplexer_7_out), .b(multiplexer_8_out), .out(adder_4_out));  // open: cin, cout
  Adder #(.width(16)) adder_5 (.a(adder_1_out), .b(adder_2_out), .out(adder_5_out));  // open: cin, cout
  Adder #(.width(16)) adder_6 (.a(adder_3_out), .b(adder_4_out), .out(adder_6_out));  // open: cin, cout
  Adder #(.width(16)) adder_7 (.a(adder_5_out), .b(adder_6_out), .out(Result));  // open: cin, cout
endmodule
