// Logisim project step-1.circ as structural Verilog: 1 circuit, main circuit main
module main (
  input  [7:0] A,
  input  [7:0] B,
  output [15:0] Result
);

  ROM #(.addrWidth(16), .dataWidth(16)) rom_1 (.addr({B, A}), .data(Result));  // open: sel

  // Notes on the sheet:
  //   contents of rom_1 (hex, n*v repeats v):
  //   257*0 1 2 3 4 5 6 7 8 9 a b c d e f 10 11 12 13 14 15 16 17 18 19 1a 1b 1c 1d 1e 1f 20 21 22 23 24
  //   25 26 27 28 29 2a 2b 2c 2d 2e 2f 30 31 32 33 34 35 36 37 38 39 3a 3b 3c 3d 3e 3f 40 41 42 43 44 45
  //   46 47 48 49 4a 4b 4c 4d 4e 4f 50 51 52 53 54 55 56 57 58 59 5a 5b 5c 5d 5e 5f 60 61 62 63 64 65 66
  //   67 68 69 6a 6b 6c 6d 6e 6f 70 71 72 73 74 75 76 77 78 79 7a 7b 7c 7d 7e 7f 80 81 82 83 84 85 86 87
  //   88 89 8a 8b 8c 8d 8e 8f 90 91 92 93 94 95 96 97 98 99 9a 9b 9c 9d 9e 9f a0 a1 a2 a3 a4 a5 a6 a7 a8
  //   a9 aa ab ac ad ae af b0 b1 b2 b3 b4 b5 b6 b7 b8 b9 ba bb bc bd be bf c0 c1 c2 c3 c4 c5 c6 c7 c8 c9
  //   ca cb cc cd ce cf d0 d1 d2 d3 d4 d5 d6 d7 d8 d9 da db dc dd de df e0 e1 e2 e3 e4 e5 e6 e7 e8 e9 ea
  //   eb ec ed ee ef f0 f1 f2 f3 f4 f5 f6 f7 f8 f9 fa fb fc fd fe ff 0 2 4 6 8 a c e 10 12 14 16 18 1a 1c
  //   1e 20 22 24 26 28 2a 2c 2e 30 32 34 36 38 3a 3c 3e 40 42 44 46 48 4a 4c 4e 50 52 54 56 58 5a 5c 5e
  //   60 62 64 66 68 6a 6c 6e 70 72 74 76 78 7a 7c 7e 80 82 84 86 88 8a 8c 8e 90 92 94 96 98 9a 9c 9e a0
  //   a2 a4 a6 a8 aa ac ae b0 b2 b4 b6 b8 ba bc be c0 c2 c4 c6 c8 ca cc ce d0 d2 d4 d6 d8 da dc de e0 e2
  //   e4 e6 e8 ea ec ee f0 f2 f4 f6 f8 fa fc fe 100 102 104 106 108 10a 10c 10e 110 112 114 116 118 11a
  //   11c 11e 120 122 124 126 128 12a 12c 12e 130 132 134 136 138 13a 13c 13e 140 142 144 146 148 14a 14c
  //   14e 150 152 154 156 158 15a 15c 15e 160 162 164 166 168 16a 16c 16e 170 172 174 176 178 17a 17c 17e
  //   180 182 184 186 188 18a 18c 18e 190 192 194 196 198 19a 19c 19e 1a0 1a2 1a4 1a6 1a8 1aa 1ac 1ae 1b0
  //   1b2 1b4 1b6 1b8 1ba 1bc 1be 1c0 1c2 1c4 1c6 1c8 1ca 1cc 1ce 1d0 1d2 1d4 1d6 1d8 1da 1dc 1de 1e0 1e2
  //   1e4 1e6 1e8 1ea 1ec 1ee 1f0 1f2 1f4 1f6 1f8 1fa 1fc 1fe 0 3 6 9 c f 12 15 18 1b 1e 21 24 27 2a 2d 30
  //   33 36 39 3c 3f 42 45 48 4b 4e 51 54 57 5a 5d 60 63 66 69 6c 6f 72 75 78 7b 7e 81 84 87 8a 8d 90 93
  //   96 99 9c 9f a2 a5 a8 ab ae b1 b4 b7 ba bd c0 c3 c6 c9 cc cf d2 d5 d8 db de e1 e4 e7 ea ed f0 f3 f6
  //   f9 fc ff 102 105 108 10b 10e 111 114 117 11a 11d 120 123 126 129 12c 12f 132 135 138 13b 13e 141 144
  //   147 14a 14d 150 153 156 159 15c 15f 162 165 168 16b 16e 171 174 177 17a 17d 180 183 186 189 18c 18f
  //   192 195 198 19b 19e 1a1 1a4 1a7 1aa 1ad 1b0 1b3 1b6 1b9 1bc 1bf 1c2 1c5 1c8 1cb 1ce 1d1 1d4 1d7 1da
  //   1dd 1e0 1e3 1e6 1e9 1ec 1ef 1f2 1f5 1f8 1fb 1fe 201 204 207 20a 20d 210 213 216 219 21c 21f 222 225
  //   228 22b 22e 231 234 237 23a 23d 240 243 246 249 24c 24f 252 255 258 25b 25e 261 264 267 26a 26d 270
  //   273 276 279 27c 27f 282 285 288 28b 28e 291 294 297 29a 29d 2a0 2a3 2a6 2a9 2ac 2af 2b2 2b5 2b8 2bb
  //   2be 2c1 2c4 2c7 2ca 2cd 2d0 2d3 2d6 2d9 2dc 2df 2e2 2e5 2e8 2eb 2ee 2f1 2f4 2f7 2fa 2fd 0 4 8 c 10
  //   14 18 1c 20 24 28 2c 30 34 38 3c 40 44 48 4c 50 54 58 5c 60 64 68 6c 70 74 78 7c 80 84 88 8c 90 94
  //   98 9c a0 a4 a8 ac b0 b4 b8 bc c0 c4 c8 cc d0 d4 d8 dc e0 e4 e8 ec f0 f4 f8 fc 100 104 108 10c 110
  //   114 118 11c 120 124 128 12c 130 134 138 13c 140 144 148 14c 150 154 158 15c 160 164 168 16c 170 174
  //   178 17c 180 184 188 18c 190 194 198 19c 1a0 1a4 1a8 1ac 1b0 1b4 1b8 1bc 1c0 1c4 1c8 1cc 1d0 1d4 1d8
  //   1dc 1e0 1e4 1e8 1ec 1f0 1f4 1f8 1fc 200 204 208 20c 210 214 218 21c 220 224 228 22c 230 234 238 23c
  //   240 244 248 24c 250 254 258 25c 260 264 268 26c 270 274 278 27c 280 284 288 28c 290 294 298 29c 2a0
  //   2a4 2a8 2ac 2b0 2b4 2b8 2bc 2c0 2c4 2c8 2cc 2d0 2d4 2d8 2dc 2e0 2e4 2e8 2ec 2f0 2f4 2f8 2fc 300 304
  //   308 30c 310 314 318 31c 320 324 328 32c 330 334 338 33c 340 344 348 34c 350 354 358 35c 360 364 368
  //   36c 370 374 378 37c 380 384 388 38c 390 394 398 39c 3a0 3a4 3a8 3ac 3b0 3b4 3b8 3bc 3c0 3c4 3c8 3cc
  //   3d0 3d4 3d8 3dc 3e0 3e4 3e8 3ec 3f0 3f4 3f8 3fc 0 5 a f 14 19 1e 23 28 2d 32 37 3c 41 46 4b 50 55 5a
  //   5f 64 69 6e 73 78 7d 82 87 8c 91 96 9b a0 a5 aa af b4 b9 be c3 c8 cd d2 d7 dc e1 e6 eb f0 f5 fa ff
  //   104 109 10e 113 118 11d 122 127 12c 131 136 13b 140 145 14a 14f 154 159 15e 163 168 16d 172 177 17c
  //   181 186 18b 190 195 19a 19f 1a4 1a9 1ae 1b3 1b8 1bd 1c2 1c7 1cc 1d1 1d6 1db 1e0 1e5 1ea 1ef 1f4 1f9
  //   1fe 203 208 20d 212 217 21c 221 226 22b 230 235 23a 23f 244 249 24e 253 258 25d 262 267 26c 271 276
  //   27b 280 285 28a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
endmodule
